// Digital circuit CPU8Bit32i.dig as structural Verilog
module CPU8Bit32i (
  input  RST,
  input  Clock,
  input  [7:0] BusIn,
  input  [7:0] PromIN,
  input  [7:0] RamIn,
  output [7:0] BusOut,
  output [7:0] AddrBus,
  output OutE,
  output InE,
  output [7:0] PC,
  output RamE,
  output RamOe
);

  wire AE, and_1_out, BE, BusMux0, BusMux1, BusMux2, C, CCLR, CE, Cout, CSET, E, G, IRZ, JMP,
       multiplexer_1_out, N, OP0, OP1, OP2, RamAMux, S, Z;
  wire [4:0] IR;
  wire [7:0] A, alu8bits8f_1_y, B;

  ROM #(.AddrBits(5), .Bits(18)) CtrlROM (
    .A(IR), .sel(1'b1),
    .D({CCLR, CE, CSET, BE, AE, OutE, InE, JMP, OP2, OP1, OP0, RamE, RamOe, RamAMux, IRZ, BusMux2, BusMux1, BusMux0}));
  Multiplexer #(.Selector_Bits(3)) multiplexer_1 (
    .sel({OP2, OP1, OP0}), .in_0(1'b0), .in_1(1'b1), .in_2(Z), .in_3(E), .in_4(G), .in_5(S), .in_6(N),
    .in_7(C), .out(multiplexer_1_out));
  and and_1 (and_1_out, JMP, multiplexer_1_out);
  PC pc_1 (.L(and_1_out), .R(RST), .nCLK(Clock), .D(PromIN), .Q(PC));
  Reg8 reg8_1 (.E(AE), .CLK(Clock), .D(BusOut), .Q(A));
  Reg1 reg1_1 (.Q(C), .CLR(CCLR), .S(CSET), .D(Cout), .CLK(Clock), .E(CE));
  ALU8Bits8f alu8bits8f_1 (.Y(alu8bits8f_1_y), .A(A), .B(B), .ST({Cout, N, S, G, E, Z}), .OPC({C, OP2, OP1, OP0}));
  Reg5 reg5_1 (.D(PromIN[4:0]), .Q(IR), .SR(IRZ), .nCLK(Clock));
  Reg8 reg8_2 (.E(BE), .CLK(Clock), .D(BusOut), .Q(B));
  Multiplexer #(.Selector_Bits(3), .Bits(8)) multiplexer_2 (
    .sel({BusMux2, BusMux1, BusMux0}), .in_0(alu8bits8f_1_y), .in_1(RamIn), .in_2(BusIn), .in_3(PromIN),
    .in_4(A), .in_5(B), .in_6({8{1'b0}}), .in_7({8{1'b0}}), .out(BusOut));
  Multiplexer #(.Bits(8)) multiplexer_3 (.sel(RamAMux), .in_0(B), .in_1(PromIN), .out(AddrBus));

  // Other names for the same wires on the sheet: BUS[7:0] = BusOut; CLK = Clock; PROM[7:0] = PromIN; RESET = RST

  // Notes on the sheet:
  //   RST: default 1
  //   Clock: Hz: 10
  //   contents of CtrlROM (hex, n*v repeats v):
  //   0,200b,400b,4004,2005,44,5c,5d,2021,2039,4039,2802,281a,1004,101c
  //   ,488,508,588,608,688,708,788,18000,30000,2000,2080,2100,2180,12200
  //   ,12280,12300,12380
endmodule
