// Digital circuit CPU8Bit32iTESTE.dig as structural Verilog
module CPU8Bit32iTESTE (
  input  Dip4,
  input  Dip1,
  input  Dip2,
  input  Dip3,
  input  S1,
  input  S2,
  input  S3,
  input  reserv,
  input  RST,
  input  Clock,
  output [7:0] out0,
  output [7:0] out1
);

  wire AE, and_1_out, and_2_out, and_3_out, BE, BMux0, BMux1, C, CE, Cout, E, G, IRZ, JMP, multiplexer_1_out,
       N, not_1_out, OP0, OP1, OP2, OP3, OUTE, p1, p2, PcASel, RamE, S, Z;
  wire [1:0] multiplexer_4_out;
  wire [4:0] IR;
  wire [7:0] A, alu8bits8f_1_y, B, BUS, multiplexer_3_out, PC, PROM, RAMD;
  wire [7:2] multiplexer_4_out_2;
  wire [15:0] d1, d2, d3, d4, d5, d6, d7, d8, d9;

  ROM #(.AddrBits(8), .Bits(8)) rom_1 (.A(multiplexer_3_out), .sel(1'b1), .D(PROM));
  Control control_1 (
    .in(IR), .CLK(Clock), ._0(BMux0), ._1(BMux1), ._2(PcASel), ._3(IRZ), ._4(RamE), ._5(OP0), ._6(OP1),
    ._7(OP2), ._8(OP3), ._9(JMP), ._10(OUTE), ._11(AE), ._12(BE), ._13(CE));
  Multiplexer #(.Selector_Bits(3)) multiplexer_1 (
    .sel({OP2, OP1, OP0}), .in_0(1'b0), .in_1(1'b1), .in_2(Z), .in_3(E), .in_4(G), .in_5(S), .in_6(N),
    .in_7(C), .out(multiplexer_1_out));
  Reg5 u_IR (.D(PROM[4:0]), .Q(IR), .SR(IRZ), .nCLK(Clock));
  and and_1 (and_1_out, multiplexer_1_out, JMP);
  Reg8 u_A (.E(AE), .CLK(Clock), .D(BUS), .Q(A));
  ALU8Bits8f alu8bits8f_1 (.Y(alu8bits8f_1_y), .A(A), .B(B), .ST({Cout, N, S, G, E, Z}), .OPC({C, OP3, OP2, OP1, OP0}));
  Register u_C (.D(Cout), .C(Clock), .en(CE), .Q(C));
  PC u_PC (.L(and_1_out), .R(RST), .nCLK(Clock), .D(BUS), .Q(PC));
  Reg8 u_B (.E(BE), .CLK(Clock), .D(BUS), .Q(B));
  Multiplexer #(.Selector_Bits(2), .Bits(8)) multiplexer_2 (
    .sel({BMux1, BMux0}), .in_0(alu8bits8f_1_y), .in_1(RAMD),
    .in_2({reserv, S3, S2, S1, Dip1, Dip2, Dip3, Dip4}), .in_3(PROM), .out(BUS));
  Multiplexer #(.Bits(8)) multiplexer_3 (.sel(PcASel), .in_0(B), .in_1(PC), .out(multiplexer_3_out));
  Multiplexer #(.Bits(8)) multiplexer_4 (
    .sel(IRZ), .in_0(B), .in_1(PROM), .out({multiplexer_4_out_2, multiplexer_4_out}));
  InROM inrom_1 (
    .in(IR), .IRZ(IRZ), ._1(d1), ._2(d2), ._3(d3), ._4(d4), ._5(d5), ._6(p1), ._7(d6), ._8(d7), ._9(p2),
    ._10(d8), ._11(d9));
  not not_1 (not_1_out, multiplexer_4_out[0]);
  LED led_1 (.in(C));
  and and_2 (and_2_out, not_1_out, OUTE);
  and and_3 (and_3_out, multiplexer_4_out[0], OUTE);
  Seven_Seg_Hex seven_seg_hex_1 (.d(A[7:4]), .dp(1'b0));
  RAMDualPort #(.Bits(8)) ramdualport_1 (.A(multiplexer_4_out), .Din(BUS), .str(RamE), .C(Clock), .ld(1'b1), .D(RAMD));
  Register #(.Bits(8)) register_1 (.D(BUS), .C(Clock), .en(and_2_out), .Q(out0));
  Register #(.Bits(8)) register_2 (.D(BUS), .C(Clock), .en(and_3_out), .Q(out1));
  SixteenSeg sixteenseg_1 (.led(d1), .dp(1'b0));
  Seven_Seg_Hex seven_seg_hex_2 (.d(A[3:0]), .dp(1'b0));
  SixteenSeg sixteenseg_2 (.led(d2), .dp(1'b0));
  Seven_Seg_Hex seven_seg_hex_3 (.d(B[7:4]), .dp(1'b0));
  LED led_2 (.in(out0[0]));
  LED led_3 (.in(out0[1]));
  SixteenSeg sixteenseg_3 (.led(d3), .dp(1'b0));
  Seven_Seg_Hex seven_seg_hex_4 (.d(B[3:0]), .dp(1'b0));
  SixteenSeg sixteenseg_4 (.led(d4), .dp(1'b0));
  Seven_Seg seven_seg_1 (
    .a(out1[0]), .b(out1[1]), .c(out1[2]), .d(out1[3]), .e(out1[4]), .f(out1[5]), .g(out1[6]), .dp(out1[7]));
  SixteenSeg sixteenseg_5 (.led(d5), .dp(1'b0));
  Seven_Seg_Hex seven_seg_hex_5 (.d({3'b000, IR[4]}), .dp(1'b0));
  LED led_4 (.in(p1));
  Seven_Seg_Hex seven_seg_hex_6 (.d(IR[3:0]), .dp(1'b0));
  SixteenSeg sixteenseg_6 (.led(d6), .dp(1'b0));
  Seven_Seg_Hex seven_seg_hex_7 (.d(PC[7:4]), .dp(1'b0));
  SixteenSeg sixteenseg_7 (.led(d7), .dp(1'b0));
  Seven_Seg_Hex seven_seg_hex_8 (.d(PC[3:0]), .dp(1'b0));
  LED led_5 (.in(p2));
  SixteenSeg sixteenseg_8 (.led(d8), .dp(1'b0));
  Seven_Seg_Hex seven_seg_hex_9 (.d(BUS[7:4]), .dp(1'b0));
  SixteenSeg sixteenseg_9 (.led(d9), .dp(1'b0));
  Seven_Seg_Hex seven_seg_hex_10 (.d(BUS[3:0]), .dp(1'b0));

  // Other names for the same wires on the sheet: CLK = Clock; a_t = out1[0]; b_t = out1[1]; c_t = out1[2];
  //   d = out1[3]; e_t = out1[4]; f = out1[5]; g_t = out1[6]; dp = out1[7]; RESET = RST

  // Notes on the sheet:
  //   Dip4: pin 58
  //   Dip1: pin 61
  //   Dip2: pin 66
  //   Dip3: pin 57
  //   S1: pin 54
  //   S2: pin 56
  //   S3: pin 55
  //   reserv: pin 100
  //   RST: default 1
  //   Clock: Hz: 10
  //   contents of rom_1 (hex, n*v repeats v):
  //   1,0,7,0,7,1,7,2,f,31,2,1,a,1,1c,7,1,2,ff,13,a,2,1,a,0,1c,7,0,2
  //   ,1e,13,a,1,0,7,0,2,1,a,2,1c,2,a,13,2f,1,0,7,2,2,3a,1c,4,3,d,1
  //   ,f,a,3f,6,5b,4f,66,6d,7d,7,7f,6f,77,7c,39,5e,79,71
  //   A
  //   B
  //   IR
  //   PC
  //   BUS
endmodule
