// Digital circuit ALU8Bits8f.dig as structural Verilog
module ALU8Bits8f (
  input  [7:0] A,
  input  [7:0] B,
  input  [4:0] OPC,
  output [7:0] Y,
  output [5:0] ST
);

  wire [7:0] add_1_s, and_1_out, not_1_out, or_1_out, sub_1_s, xor_1_out;
  wire [8:0] lsl8_1_do, lsr8_1_do;
  wire [8:8] add_1_c_o, sub_1_c_o;

  Comparator #(.Bits(8)) comparator_1 (.a(A), .b({8{1'b0}}), .eq(ST[0]), .lt(ST[4]));  // open: gt
  Comparator #(.Bits(8)) comparator_2 (.a(A), .b(B), .gt(ST[2]), .eq(ST[1]), .lt(ST[3]));
  assign not_1_out = ~A;  // Not not_1, 8 bits wide
  assign or_1_out = A | B;  // Or or_1, 8 bits wide
  assign and_1_out = A & B;  // And and_1, 8 bits wide
  assign xor_1_out = A ^ B;  // XOr xor_1, 8 bits wide
  Add #(.Bits(8)) add_1 (.a(A), .b(B), .c_i(OPC[4]), .s(add_1_s), .c_o(add_1_c_o[8]));
  Sub #(.Bits(8)) sub_1 (.a(A), .b(B), .c_i(OPC[4]), .s(sub_1_s), .c_o(sub_1_c_o[8]));
  LSL8 lsl8_1 (.Di(A), .Ci(OPC[4]), .Do(lsl8_1_do[7:0]), .Co(lsl8_1_do[8]));
  LSR8 lsr8_1 (.Di(A), .Ci(OPC[4]), .Do(lsr8_1_do[7:0]), .Co(lsr8_1_do[8]));
  Multiplexer #(.Selector_Bits(4), .Bits(9)) multiplexer_1 (
    .sel(OPC[3:0]), .in_0({1'b0, not_1_out}), .in_1({1'b0, or_1_out}), .in_2({1'b0, and_1_out}),
    .in_3({1'b0, xor_1_out}), .in_4({add_1_c_o[8], add_1_s}), .in_5({sub_1_c_o[8], sub_1_s}),
    .in_6(lsl8_1_do), .in_7(lsr8_1_do), .in_8({1'b0, A}), .in_9({1'b1, B}), .in_10({9{1'b0}}),
    .in_11({9{1'b0}}), .in_12({9{1'b0}}), .in_13({9{1'b0}}), .in_14({9{1'b0}}), .in_15({9{1'b0}}),
    .out({ST[5], Y}));

  // Other names for the same wires on the sheet: C = ST[5]; E = ST[1]; G = ST[2]; N = ST[4]; OP[3:0] = OPC[3:0];
  //   S = ST[3]; Z = ST[0]
endmodule
