// Digital circuit CtrlRom.dig as structural Verilog
module CtrlRom (
  input  [4:0] in,
  output _0,
  output _1,
  output _2,
  output _3,
  output _4,
  output _5,
  output _6,
  output _7,
  output _8,
  output _9,
  output _10,
  output _11,
  output _12,
  output _13,
  output _14,
  output _15
);

  wire and_1_out, and_2_out, and_3_out, and_4_out, and_5_out, and_6_out, and_7_out, and_8_out, and_9_out,
       and_10_out, and_11_out, and_12_out, and_13_out, and_14_out, and_15_out, and_16_out, and_17_out,
       and_18_out, and_19_out, and_20_out, and_21_out, and_22_out, and_23_out, and_24_out, and_25_out,
       and_26_out, and_27_out, and_28_out, and_29_out, and_30_out, and_31_out, and_32_out, and_33_out,
       and_34_out, and_35_out, and_36_out, and_38_out, and_39_out, and_40_out, and_41_out, and_42_out,
       and_43_out, and_44_out, and_45_out, and_46_out, and_48_out, and_49_out, not_1_out, not_2_out,
       not_3_out, not_4_out, not_5_out;

  not not_1 (not_1_out, in[4]);
  not not_2 (not_2_out, in[3]);
  not not_3 (not_3_out, in[2]);
  not not_4 (not_4_out, in[1]);
  not not_5 (not_5_out, in[0]);
  and and_1 (and_1_out, not_1_out, in[3], in[1]);
  and and_2 (and_2_out, in[4], not_2_out, not_4_out);
  and and_3 (and_3_out, not_1_out, in[3], not_3_out);
  and and_4 (and_4_out, in[4], not_2_out, not_3_out);
  and and_5 (and_5_out, not_2_out, not_3_out, in[1], not_5_out);
  and and_6 (and_6_out, not_2_out, not_4_out, in[0]);
  and and_7 (and_7_out, not_1_out, in[3], in[2], not_4_out, not_5_out);
  and and_8 (and_8_out, not_1_out, in[3], in[2], in[1], in[0]);
  and and_9 (and_9_out, in[4], not_2_out, not_4_out);
  and and_10 (and_10_out, not_2_out, not_3_out, in[0]);
  and and_11 (and_11_out, not_2_out, not_3_out, in[1]);
  and and_12 (and_12_out, not_1_out, in[3], not_3_out, not_4_out, not_5_out);
  and and_13 (and_13_out, not_1_out, in[2], not_4_out, in[0]);
  and and_14 (and_14_out, not_1_out, in[2], in[1], not_5_out);
  and and_15 (and_15_out, not_1_out, not_2_out, in[1], in[0]);
  and and_16 (and_16_out, not_1_out, not_2_out, in[2]);
  and and_17 (and_17_out, not_1_out, not_3_out, in[1], not_5_out);
  and and_18 (and_18_out, not_1_out, in[2], in[1], in[0]);
  and and_19 (and_19_out, not_1_out, in[3], not_4_out, not_5_out);
  and and_20 (and_20_out, not_1_out, in[3], not_3_out, in[1]);
  and and_21 (and_21_out, not_1_out, in[3], in[2], not_4_out);
  and and_22 (and_22_out, in[4], not_2_out, not_4_out);
  and and_23 (and_23_out, in[4], not_2_out, not_3_out);
  and and_24 (and_24_out, not_2_out, not_3_out, not_4_out, in[0]);
  and and_25 (and_25_out, in[2], in[0]);
  and and_26 (and_26_out, not_3_out, in[1]);
  and and_27 (and_27_out, not_4_out, not_5_out);
  and and_28 (and_28_out, not_1_out, in[3], not_3_out, not_4_out, not_5_out);
  and and_29 (and_29_out, not_1_out, not_2_out, in[2], in[1]);
  or or_1 (_6, not_1_out, in[0]);
  and and_30 (and_30_out, in[4], in[3], in[1]);
  and and_31 (and_31_out, not_2_out, not_4_out);
  and and_32 (and_32_out, in[4], in[2]);
  and and_33 (and_33_out, not_2_out, in[1]);
  and and_34 (and_34_out, not_1_out, in[3], in[2], in[1]);
  and and_35 (and_35_out, in[4], not_2_out, not_3_out);
  and and_36 (and_36_out, in[4], not_2_out, not_4_out);
  and and_37 (_10, not_1_out, in[3], in[2], not_4_out, in[0]);
  and and_38 (and_38_out, not_1_out, not_2_out, not_4_out, in[0]);
  and and_39 (and_39_out, not_1_out, not_2_out, not_3_out, in[0]);
  and and_40 (and_40_out, in[4], in[3]);
  and and_41 (and_41_out, in[3], not_3_out, not_4_out, in[0]);
  and and_42 (and_42_out, in[3], not_3_out, in[1], not_5_out);
  and and_43 (and_43_out, in[3], in[2], not_4_out, not_5_out);
  and and_44 (and_44_out, not_1_out, not_2_out, not_3_out, in[1], not_5_out);
  and and_45 (and_45_out, not_1_out, not_2_out, in[2], not_4_out, not_5_out);
  and and_46 (and_46_out, not_1_out, in[3], not_3_out, in[1], in[0]);
  and and_47 (_13, not_2_out, not_5_out);
  and and_48 (and_48_out, in[4], in[2], in[1]);
  and and_49 (and_49_out, in[4], in[3], in[2]);
  and and_50 (_15, not_2_out, in[0]);
  or or_2 (_4, and_25_out, and_26_out, and_27_out);
  or or_3 (_5, and_28_out, and_29_out);
  or or_4 (_7, and_30_out, and_31_out);
  or or_5 (_8, and_32_out, and_33_out);
  or or_6 (_9, and_34_out, and_35_out, and_36_out);
  or or_7 (_12, and_44_out, and_45_out, and_46_out);
  or or_8 (_14, and_48_out, and_49_out);
  or or_9 (_0, and_1_out, and_2_out, and_3_out, and_4_out, and_5_out, and_6_out);
  or or_10 (_1, and_7_out, and_8_out, and_9_out, and_10_out, and_11_out);
  or or_11 (_2, and_12_out, and_13_out, and_14_out, and_15_out, and_16_out);
  or or_12 (_3, and_17_out, and_18_out, and_19_out, and_20_out, and_21_out, and_22_out, and_23_out, and_24_out);
  or or_13 (_11, and_38_out, and_39_out, and_40_out, and_41_out, and_42_out, and_43_out);
endmodule
