// Digital circuit InROM.dig as structural Verilog
module InROM (
  input  [4:0] in,
  input  IRZ,
  output [15:0] _1,
  output [15:0] _2,
  output [15:0] _4,
  output [15:0] _3,
  output [15:0] _5,
  output _6,
  output [15:0] _7,
  output [15:0] _8,
  output _9,
  output [15:0] _10,
  output [15:0] _11
);

  wire [4:0] multiplexer_1_out;
  wire [5:5] not_1_out;

  Multiplexer #(.Bits(5)) multiplexer_1 (.sel(not_1_out[5]), .in_0(in), .in_1({5{1'b0}}), .out(multiplexer_1_out));
  not not_1 (not_1_out[5], IRZ);
  ROM #(.AddrBits(6), .Bits(48)) rom_1 (.A({not_1_out[5], multiplexer_1_out}), .sel(1'b1), .D({_3, _2, _1}));
  ROM #(.AddrBits(6), .Bits(33)) rom_2 (.A({not_1_out[5], multiplexer_1_out}), .sel(1'b1), .D({_6, _5, _4}));
  ROM #(.AddrBits(6), .Bits(33)) rom_3 (.A({not_1_out[5], multiplexer_1_out}), .sel(1'b1), .D({_9, _8, _7}));
  ROM #(.AddrBits(6), .Bits(32)) rom_4 (.A({not_1_out[5], multiplexer_1_out}), .sel(1'b1), .D({_11, _10}));

  // Notes on the sheet:
  //   contents of rom_1 (hex, n*v repeats v):
  //   3c700ff24cc,37c00f0,37c00f0,37c00f0,90c000ff14cc,90c000ff14cc
  //   ,23c7a0cc,23c7a0cc,23c7a0cc,37c23c7,37c23c7,37c23c7,24cc00c0,480300fc00ff
  //   ,3c714cc007c,3c714cc007c,9033000c007c,3f3000c007c,2fb000c007c
  //   ,3bb000c007c,24cc000c007c,f3000c007c,480303f303bb,23c700f000f3
  //   ,480300ff24cc,23c700ff,37c24cc03cf,23c700ffb400,37c037c03cf,3f800fc03bb
  //   ,f003bb00f0,23c703bb00f0,30003000300
  //   contents of rom_2 (hex, n*v repeats v):
  //   0,1000003cf,1000003f8,1000003cf,1000003f8,1000003cf,1000003f8
  //   ,1037c03cf,1037c03cf,1000003cf,1000003cf,1000003f8,1000003cf,1037c03cf
  //   ,3f8,37c03cf,5*1000003cf,37c03cf,f3,f3,3cf,5*1000003cf,3cf,3cf
  //   contents of rom_3 (hex, n*v repeats v):
  //   0,3cf90c0,3cf90c0,3f8,3cf,3f8,3cf,3cf,3f8,3f8,37c03cf,37c03cf,37c03cf
  //   ,3cf,0,0,37c03cf,1000003f8,1000003f8,1000003f8,37c03cf,4*0,5*3f8
  //   contents of rom_4 (hex, n*v repeats v):
  //   17*0,37c03cf,37c03cf,37c03cf
endmodule
