// Digital circuit LSL8.dig as structural Verilog
module LSL8 (
  input  [7:0] Di,
  input  Ci,
  output [7:0] Do,
  output Co
);


  assign Co = Di[7];
  assign Do = {Di[6:0], Ci};

  // Notes on the sheet:
  //   Di: data input
  //   {{de Dateneingang}}
  //   Ci: carry input
  //   {{de Carry-Eingang}}
  //   Do: data output
  //   Co: carry output
  //   {{de Carry-Ausgang}}
endmodule
