// Digital circuit PC.dig as structural Verilog
module PC (
  input  L,
  input  nCLK,
  input  [7:0] D,
  input  R,
  output [7:0] Q
);

  wire [7:0] add_1_s, multiplexer_1_out, multiplexer_2_out;

  Multiplexer #(.Bits(8)) multiplexer_1 (.sel(R), .in_0(multiplexer_2_out), .in_1({8{1'b0}}), .out(multiplexer_1_out));
  Multiplexer #(.Bits(8)) multiplexer_2 (.sel(L), .in_0(add_1_s), .in_1(D), .out(multiplexer_2_out));
  Register #(.Bits(8)) register_1 (.D(multiplexer_1_out), .C(~nCLK), .en(1'b1), .Q(Q));
  Add #(.Bits(8)) add_1 (.a(Q), .b(8'h1), .c_i(1'b0), .s(add_1_s));  // open: c_o
endmodule
