// Digital circuit Reg1.dig as structural Verilog
module Reg1 (
  input  E,
  input  CLK,
  input  CLR,
  input  D,
  input  S,
  output Q
);

  wire multiplexer_1_out, or_1_out;

  or or_1 (or_1_out, CLR, S);
  Multiplexer multiplexer_1 (.sel(or_1_out), .in_0(D), .in_1(S), .out(multiplexer_1_out));
  Register register_1 (.D(multiplexer_1_out), .C(CLK), .en(E), .Q(Q));
endmodule
