// Digital circuit Reg5.dig as structural Verilog
module Reg5 (
  input  [4:0] D,
  input  nCLK,
  input  SR,
  output [4:0] Q
);

  wire [4:0] multiplexer_1_out;

  Multiplexer #(.Bits(5)) multiplexer_1 (.sel(SR), .in_0(D), .in_1({5{1'b0}}), .out(multiplexer_1_out));
  D_FF #(.Bits(5)) d_ff_1 (.D(multiplexer_1_out), .C(~nCLK), .Q(Q));  // open: nQ
endmodule
