// Digital circuit Reg8.dig as structural Verilog
module Reg8 (
  input  E,
  input  CLK,
  input  [7:0] D,
  output [7:0] Q
);

  Register #(.Bits(8)) register_1 (.D(D), .C(CLK), .en(E), .Q(Q));
endmodule
