// Digital circuit CpuExternalRam.dig as structural Verilog
module CpuExternalRam (
  input  Dip4,
  input  Clock,
  input  Dip1,
  input  Dip2,
  input  Dip3,
  input  S1,
  input  S2,
  input  S3,
  input  reserv,
  input  [7:0] PromIn,
  output InE,
  output [7:0] out0,
  output [7:0] out1,
  output [7:0] PC,
  output WE,
  output OE,
  output [7:0] Addr,
  output [7:0] RamIn
);

  wire and_1_out, and_2_out, cpu8bit32i_1_oute, not_1_out;
  wire [7:0] pincontrol_1_p1, pincontrol_1_p3;

  // PinControl #(.Bits(8)) pincontrol_1: pin names not known; wires that end beside it: pincontrol_1_p1, OE, pincontrol_1_p3, RamIn
  CPU8Bit32i cpu8bit32i_1 (
    .RST(1'b0), .Clock(Clock), .BusIn({reserv, S3, S2, S1, Dip1, Dip2, Dip3, Dip4}), .PromIN(PromIn),
    .RamIn(pincontrol_1_p3), .BusOut(pincontrol_1_p1), .AddrBus(Addr), .OutE(cpu8bit32i_1_oute), .PCaddr(PC),
    .RamE(OE));
  not not_1 (not_1_out, Addr[0]);
  not not_2 (WE, OE);
  and and_1 (and_1_out, not_1_out, cpu8bit32i_1_oute);
  and and_2 (and_2_out, Addr[0], cpu8bit32i_1_oute);
  Register #(.Bits(8)) register_1 (.D(pincontrol_1_p1), .C(Clock), .en(and_1_out), .Q(out0));
  Register #(.Bits(8)) register_2 (.D(pincontrol_1_p1), .C(Clock), .en(and_2_out), .Q(out1));

  assign InE = 1'b0;

  // Notes on the sheet:
  //   Dip4: pin 58
  //   Clock: pin 81, Hz: 10
  //   InE: pin 92
  //   out0: pin 67,68,78,82,84,86,88,90
  //   out1: pin 75,73,71,70,72,76,74,69
  //   Dip1: pin 61
  //   Dip2: pin 66
  //   Dip3: pin 57
  //   S1: pin 54
  //   S2: pin 56
  //   S3: pin 55
  //   reserv: pin 100
endmodule
