// Digital circuit CpuRamRom.dig as structural Verilog
module CpuRamRom (
  input  Dip4,
  input  Clock,
  input  Dip1,
  input  Dip2,
  input  Dip3,
  input  S1,
  input  S2,
  input  S3,
  input  reserv,
  output InE,
  output [7:0] out0,
  output [7:0] out1
);

  wire and_1_out, and_2_out, cpu8bit32i_1_oute, cpu8bit32i_1_rame, not_1_out;
  wire [1:0] cpu8bit32i_1_addrbus;
  wire [7:0] cpu8bit32i_1_busout, cpu8bit32i_1_pcaddr, ramdualport_1_d, rom_1_d;
  wire [7:2] cpu8bit32i_1_addrbus_2;

  ROM #(.AddrBits(8), .Bits(8)) rom_1 (.A(cpu8bit32i_1_pcaddr), .sel(1'b1), .D(rom_1_d));
  CPU8Bit32i cpu8bit32i_1 (
    .RST(1'b0), .Clock(Clock), .BusIn({reserv, S3, S2, S1, Dip1, Dip2, Dip3, Dip4}), .PromIN(rom_1_d),
    .RamIn(ramdualport_1_d), .BusOut(cpu8bit32i_1_busout),
    .AddrBus({cpu8bit32i_1_addrbus_2, cpu8bit32i_1_addrbus}), .OutE(cpu8bit32i_1_oute),
    .PCaddr(cpu8bit32i_1_pcaddr), .RamE(cpu8bit32i_1_rame));
  not not_1 (not_1_out, cpu8bit32i_1_addrbus[0]);
  and and_1 (and_1_out, not_1_out, cpu8bit32i_1_oute);
  and and_2 (and_2_out, cpu8bit32i_1_addrbus[0], cpu8bit32i_1_oute);
  RAMDualPort #(.Bits(8)) ramdualport_1 (
    .A(cpu8bit32i_1_addrbus), .Din(cpu8bit32i_1_busout), .str(cpu8bit32i_1_rame), .C(Clock), .ld(1'b1),
    .D(ramdualport_1_d));
  Register #(.Bits(8)) register_1 (.D(cpu8bit32i_1_busout), .C(Clock), .en(and_1_out), .Q(out0));
  Register #(.Bits(8)) register_2 (.D(cpu8bit32i_1_busout), .C(Clock), .en(and_2_out), .Q(out1));
  LED led_1 (.in(out0[0]));
  LED led_2 (.in(out0[1]));
  Seven_Seg seven_seg_1 (
    .a(out1[0]), .b(out1[1]), .c(out1[2]), .d(out1[3]), .e(out1[4]), .f(out1[5]), .g(out1[6]), .dp(out1[7]));

  assign InE = 1'b0;

  // Other names for the same wires on the sheet: a = out1[0]; b = out1[1]; c = out1[2]; d = out1[3]; e = out1[4];
  //   f = out1[5]; g = out1[6]; dp = out1[7]

  // Notes on the sheet:
  //   Dip4: pin 58
  //   Clock: pin 81, Hz: 1000
  //   InE: pin 92
  //   out0: pin 67,68,78,82,84,86,88,90
  //   out1: pin 75,73,71,70,72,76,74,69
  //   Dip1: pin 61
  //   Dip2: pin 66
  //   Dip3: pin 57
  //   S1: pin 54
  //   S2: pin 56
  //   S3: pin 55
  //   reserv: pin 100
  //   contents of rom_1 (hex, n*v repeats v):
  //   c,0,7,0,2,f,1a,7,1,a,0,1f,17,1f,17,1f,17,1f,d,0,2,3,12,1c,f,22
  //   ,f,0,1,40,d,1,f,0,a,1,2,2d,1c,4,3,d,1,f,1a,3f,6,5b,4f,66,6d,7d
  //   ,7,7f,6f,77,7c,39,5e,79,71
endmodule
