// Digital circuit mux2x8.dig as structural Verilog
module mux2x8 (
  input  [7:0] A1,
  input  [7:0] A0,
  input  s,
  output [7:0] y
);

  wire [7:0] and_1_out, and_2_out;
  wire [7:7] not_1_out;

  not not_1 (not_1_out[7], s);
  assign and_1_out = A1 & {8{s}};  // And and_1, 8 bits wide
  assign and_2_out = A0 & {8{not_1_out[7]}};  // And and_2, 8 bits wide
  assign y = and_1_out | and_2_out;  // Or or_1, 8 bits wide
endmodule
